# Fritzing sketch compass-belt (saved by Fritzing 0.9.10b)
stripboards: 1

parts:
  U1 = Vibration Motor- ROB-08449 [package=vibe-motor-10mm]
  IC2 = ULN2803A [package=THT]
  U2 = Vibration Motor- ROB-08449 [package=vibe-motor-10mm]
  U3 = Vibration Motor- ROB-08449 [package=vibe-motor-10mm]
  U4 = Vibration Motor- ROB-08449 [package=vibe-motor-10mm]
  U5 = Vibration Motor- ROB-08449 [package=vibe-motor-10mm]
  U6 = Vibration Motor- ROB-08449 [package=vibe-motor-10mm]
  U7 = Vibration Motor- ROB-08449 [package=vibe-motor-10mm]
  U8 = Vibration Motor- ROB-08449 [package=vibe-motor-10mm]
  U9 = Vibration Motor- ROB-08449 [package=vibe-motor-10mm]
  U10 = Vibration Motor- ROB-08449 [package=vibe-motor-10mm]
  U11 = Vibration Motor- ROB-08449 [package=vibe-motor-10mm]
  U12 = Vibration Motor- ROB-08449 [package=vibe-motor-10mm]
  U13 = Vibration Motor- ROB-08449 [package=vibe-motor-10mm]
  U14 = Vibration Motor- ROB-08449 [package=vibe-motor-10mm]
  U15 = Vibration Motor- ROB-08449 [package=vibe-motor-10mm]
  U16 = Vibration Motor- ROB-08449 [package=vibe-motor-10mm]
  part = Raspberry Pi Pico
  part_2 = Electrolytic Capacitor [capacitance=220µF voltage=35V package="200 mil [THT, electrolytic]"]
  part_3 = Ceramic Capacitor [capacitance=100nF voltage=35V package="100 mil [THT, multilayer]"]
  part_4 = Ceramic Capacitor [capacitance=100nF voltage=35V package="100 mil [THT, multilayer]"]
  IC1 = ULN2803A [package=THT]

nets:
  N1: U1.+, IC2.Out_1
  N2: U1.-, IC2.COM_-_Common, U2.-, U3.-, U4.-, U5.-, U6.-, U7.-, U8.-, U9.-, U10.-, U11.-, U12.-, U13.-, U14.-, U15.-, U16.-, part.pin_36, part_2.+, part_3.0, part_4.0, IC1.COM_-_Common
  N3: IC2.In_1, part.pin_10
  N4: IC2.In_2, part.pin_9
  N5: IC2.In_3, part.pin_7
  N6: IC2.In_4, part.pin_6
  N7: IC2.In_5, part.pin_5
  N8: IC2.In_6, part.pin_4
  N9: IC2.In_7, part.pin_2
  N10: IC2.In_8, part.pin_1
  N11: IC2.0V, part.pin_3, part.pin_8, part.pin_38, part_2.-, part_3.1, part_4.1, IC1.0V
  N12: IC2.Out_8, U8.+
  N13: IC2.Out_7, U7.+
  N14: IC2.Out_6, U6.+
  N15: IC2.Out_5, U5.+
  N16: IC2.Out_4, U4.+
  N17: IC2.Out_3, U3.+
  N18: IC2.Out_2, U2.+
  N19: U9.+, IC1.Out_1
  N20: U10.+, IC1.Out_2
  N21: U11.+, IC1.Out_3
  N22: U12.+, IC1.Out_4
  N23: U13.+, IC1.Out_5
  N24: U14.+, IC1.Out_6
  N25: U15.+, IC1.Out_7
  N26: U16.+, IC1.Out_8
  N27: part.pin_11, IC1.In_8
  N28: part.pin_12, IC1.In_7
  N29: part.pin_14, IC1.In_6
  N30: part.pin_15, IC1.In_5
  N31: part.pin_16, IC1.In_4
  N32: part.pin_17, IC1.In_3
  N33: part.pin_19, IC1.In_2
  N34: part.pin_20, IC1.In_1

custom parts:
  Raspberry Pi Pico: Raspberry Pi Pico. Based around the RP2040 microcontroller the Pico is a low cost microcontroller device bringing Raspberry Pi quality, cost, and easy of use to the microcontroller space. Jan 2021, Split part in to two versions: tht (this one) and SMD. This one will drill holes for a .1 in header in pcb to allow plugging in the module as well as providing pads to solder the module to the top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
